// Logisim project lab3_var1.circ as structural Verilog: 1 circuit, main circuit 1
module _1 (
  input  bit4,
  input  bit3,
  input  bit2,
  input  bit1,
  input  bit0,
  output is_consonant,
  output highest_2,
  output highest_1,
  output highest_0
);

  wire and_1_out, and_2_out, and_3_out, and_4_out, and_5_out, and_6_out, and_7_out, and_8_out, and_9_out,
       not_1_out, not_2_out, not_3_out, not_4_out, not_5_out, not_6_out, not_7_out, not_8_out, not_9_out,
       not_10_out, not_11_out, not_12_out, not_13_out, not_14_out, not_15_out, not_16_out, not_17_out,
       not_18_out, not_19_out, not_20_out;

  not not_1 (not_1_out, bit4);
  not not_2 (not_2_out, bit3);
  not not_3 (not_3_out, bit2);
  not not_4 (not_4_out, bit1);
  not not_5 (not_5_out, bit4);
  not not_6 (not_6_out, bit3);
  not not_7 (not_7_out, bit1);
  not not_8 (not_8_out, bit4);
  not not_9 (not_9_out, bit2);
  not not_10 (not_10_out, bit1);
  not not_11 (not_11_out, bit4);
  not not_12 (not_12_out, bit3);
  not not_13 (not_13_out, bit1);
  not not_14 (not_14_out, bit4);
  not not_15 (not_15_out, bit4);
  not not_16 (not_16_out, bit3);
  not not_17 (not_17_out, bit4);
  not not_18 (not_18_out, bit3);
  not not_19 (not_19_out, bit2);
  not not_20 (not_20_out, bit4);
  and and_1 (and_1_out, not_1_out, not_2_out, not_3_out, not_4_out, bit0);
  and and_2 (and_2_out, not_5_out, not_6_out, bit2, not_7_out, bit0);
  and and_3 (and_3_out, not_8_out, bit3, not_9_out, not_10_out, bit0);
  and and_4 (and_4_out, not_11_out, bit3, bit2, bit1, bit0);
  and and_5 (and_5_out, bit4, not_12_out, bit2, not_13_out, bit0);
  and and_6 (and_6_out, not_14_out, bit3);
  and and_7 (and_7_out, not_15_out, not_16_out, bit2);
  and and_8 (and_8_out, not_17_out, not_18_out, not_19_out, bit1);
  and and_9 (and_9_out, not_20_out, bit3);
  nor nor_1 (is_consonant, and_1_out, and_2_out, and_3_out, and_4_out, and_5_out);
  or or_1 (highest_1, and_6_out, and_7_out);
  or or_2 (highest_0, and_8_out, and_9_out);

  assign highest_2 = bit4;

  // Notes on the sheet:
  //   ВАРИАНТ 1
  //   Проверка на согласную
  //   Вывод старшего разряда
endmodule
